# Fritzing sketch Weather-Station (saved by Fritzing 0.9.2b)
breadboards: 1

parts:
  Pi1 = Adafruit Pi Cobbler
  U1 = ATTINY13 [package=dip]
  DHT1 = DHT22 Humidity and Temperature Sensor
  BMP1 = BMP085 Breakout
  R1 = Resistor [tolerance=±5% resistance=10k package=THT]
  R2 = Resistor [tolerance=±5% resistance=10k package=THT]
  J1 = RJ45 Jack [package=rj45-8]
  R3 = Resistor [tolerance=±5% resistance=10k package=THT]
  J2 = RJ45 Jack [package=rj45-8]
  R4 = Resistor [tolerance=±5% resistance=10k package=THT]

nets:
  3V3: Pi1.3V3, DHT1.VDD, BMP1.VIN, R1.Pin_0
  N1: Pi1.5V0, U1.VCC, R2.Pin_1, J1.7, J2.7
  N2: Pi1.SDA0, BMP1.SDA
  N3: Pi1.SCL0, BMP1.SCL
  GND: Pi1.GND, U1.PB4(ADC2), U1.GND, J1.8, R3.Pin_1, R4.Pin_1
  N4: Pi1.#4, DHT1.DATA
  GND_2: Pi1.PIN9, DHT1.GND, BMP1.GND, R1.Pin_1
  N5: Pi1.#23, J1.6, R3.Pin_0
  N6: Pi1.#24, J2.6, R4.Pin_0
  N7: Pi1.MOSI, U1.PB0(MOSI)
  N8: Pi1.MISO, U1.PB1(MISO)
  N9: Pi1.SCLK, U1.PB2(SCK_ADC1)
  N10: Pi1.CE0, U1.PB5(NRES)
  N11: U1.PB3(ADC3), R2.Pin_0

custom parts:
  Adafruit Pi Cobbler: Adafruit Pi Cobbler GPIO Breakout for Raspberry Pi
  BMP085 Breakout: A breakout for the BMP085 barometric pressure and temperature sensor
